# Fritzing sketch circuit1 (saved by Fritzing 0.9.3b)
circuit board: 5.19883cm x 4.38187cm
breadboards: 1

parts:
  V1 = DC Power [voltage=5]
  IC2 = L293D [package=THT]
  U9 = Molex Picoblade Series Header [part_number=0532610519 package=Picoblade-53261-0519]
  U12 = Molex Picoblade Series Header [part_number=0532610719 package=Picoblade-53261-0719]
  IC3 = IC, DIP package, 6 pins [chip_label=MCP3221]
  R1 = Resistor [tolerance=±5% resistance=10k package="0402 [SMD]"]
  R2 = Resistor [tolerance=±5% resistance=10k package="0402 [SMD]"]
  C1 = Electrolytic Capacitor [capacitance=0.1µF package="0605 [SMD, electrolytic]"]
  C2 = Electrolytic Capacitor [capacitance=10μF package="0605 [SMD, electrolytic]"]
  U13 = Voltage Regulator - 5V [package="TO220 [THT]"]

nets:
  N1: V1.V+, IC2.+Vmotor, U13.input_voltage
  N2: IC2.Enable_1, U12.4
  N3: IC2.In_1, U12.2
  N4: IC2.Out_1_(_Controlled_by_Enable_1_), U9.3
  GND: IC2.0V, U9.5, U12.7, IC3.pin2, C1.-, C2.-, U13.GND
  N5: IC2.Out_2_(_Controlled_by_Enable_1_), U9.4
  N6: IC2.In_2, U12.3
  N7: U9.1, IC3.pin3
  N8: U9.2, U12.1, IC3.pin1, R1.Pin_1, R2.Pin_1, C1.+, C2.+, U13.output_voltage
  N9: U12.5, IC3.pin4, R2.Pin_0
  N10: U12.6, IC3.pin6, R1.Pin_0

notes:
  1 Encoder -> AIN0
  2 Encoder VDD
  3 Motor input
  4 Motor input
  5 GND
  To PI
  1 VDD
  2 GPIO4
  3 GPIO17
  4 GPIO18
  5 SDA
  6 SCL
  7 GND
